// Digital circuit 8Bit Adder.dig as structural Verilog
module _8Bit_Adder (
  input  [7:0] A,
  input  [7:0] B,
  input  SUB,
  input  INC,
  output [7:0] Q,
  output C7,
  output Co
);

  wire _7483_1_pin14, _7486_1_pin3, _7486_1_pin6, _7486_1_pin8, _7486_1_pin11, _7486_2_pin3, _7486_2_pin6,
       _7486_2_pin8, _7486_2_pin11, _74183_1__1cn_plus_1, _74183_1__2cn_plus_1, _74183_2__1cn_plus_1;

  _7486 _7486_1 (
    .pin1(B[0]), .pin2(SUB), .pin3(_7486_1_pin3), .pin4(B[1]), .pin5(SUB), .pin6(_7486_1_pin6), .pin7(1'b0),
    .pin8(_7486_1_pin8), .pin9(B[2]), .pin10(SUB), .pin11(_7486_1_pin11), .pin12(B[3]), .pin13(SUB),
    .pin14(1'b1));
  _7486 _7486_2 (
    .pin1(B[4]), .pin2(SUB), .pin3(_7486_2_pin3), .pin4(B[5]), .pin5(SUB), .pin6(_7486_2_pin6), .pin7(1'b0),
    .pin8(_7486_2_pin8), .pin9(B[6]), .pin10(SUB), .pin11(_7486_2_pin11), .pin12(B[7]), .pin13(SUB),
    .pin14(1'b1));
  DiodeBackward diodebackward_1 (.in(INC), .out(SUB));
  _7483 _7483_1 (
    .pin1(A[3]), .pin2(Q[2]), .pin3(A[2]), .pin4(_7486_1_pin8), .pin5(1'b1), .pin6(Q[1]),
    .pin7(_7486_1_pin6), .pin8(A[1]), .pin9(Q[0]), .pin10(A[0]), .pin11(_7486_1_pin3), .pin12(1'b0),
    .pin13(INC), .pin14(_7483_1_pin14), .pin15(Q[3]), .pin16(_7486_1_pin11));
  _74183 _74183_1 (
    ._2B(_7486_2_pin6), ._2Cn(_74183_1__1cn_plus_1), ._1Z(Q[4]), ._2A(A[5]), ._2Z(Q[5]),
    ._1Cn_plus_1(_74183_1__1cn_plus_1), ._1Cn(_7483_1_pin14), ._1A(A[4]), ._1B(_7486_2_pin3),
    ._2Cn_plus_1(_74183_1__2cn_plus_1), .VCC(1'b1), .GND(1'b0));
  _74183 _74183_2 (
    ._2B(_7486_2_pin11), ._2Cn(_74183_2__1cn_plus_1), ._1Z(Q[6]), ._2A(A[7]), ._2Z(Q[7]),
    ._1Cn_plus_1(_74183_2__1cn_plus_1), ._1Cn(_74183_1__2cn_plus_1), ._1A(A[6]), ._1B(_7486_2_pin8),
    ._2Cn_plus_1(C7), .VCC(1'b1), .GND(1'b0));
  _7486 _7486_3 (
    .pin1(_74183_2__1cn_plus_1), .pin2(C7), .pin3(Co), .pin4(1'b0), .pin5(1'b0), .pin7(1'b0), .pin9(1'b0),
    .pin10(1'b0), .pin12(1'b0), .pin13(1'b0), .pin14(1'b1));  // open: pin6, pin8, pin11

  // Notes on the sheet:
  //   0 -> A+B
  //   1 -> A-B
  //   these different adders were used
  //   to allow for the detection of an
  //   overflow after a subtraction,
  //   as the carry of the previous to
  //   last bit and the last bit are needed
  //   for that
  //   Carry Out
  //   Overflow
endmodule
