// Digital circuit 8Bit Comparator.dig as structural Verilog
module _8Bit_Comparator (
  input  [7:0] B,
  input  [7:0] A,
  output gt,
  output eq
);

  _74682 _74682_1 (
    .pin1(gt), .pin2(A[0]), .pin3(B[0]), .pin4(A[1]), .pin5(B[1]), .pin6(A[2]), .pin7(B[2]), .pin8(A[3]),
    .pin9(B[3]), .pin10(1'b0), .pin11(A[4]), .pin12(B[4]), .pin13(A[5]), .pin14(B[5]), .pin15(A[6]),
    .pin16(B[6]), .pin17(A[7]), .pin18(B[7]), .pin19(eq), .pin20(1'b1));
endmodule
