// Digital circuit CMD DEC.dig as structural Verilog
module CMD_DEC (
  input  [7:0] CMD_IN,
  input  [7:0] CMD_CMP,
  output CMD_EN
);

  Comparator comparator_1 (.a(CMD_IN[0]), .b(CMD_CMP[0]), .eq(CMD_EN));  // open: gt, lt
  // Pins of 1 and 8 bits meet at CMD_IN
  // Pins of 1 and 8 bits meet at CMD_CMP
endmodule
