// Digital circuit 8 By 8 Pixel Display.dig as structural Verilog
module _8_By_8_Pixel_Display (
  input  [7:0] CMD,
  input  [7:0] DAT,
  input  [15:0] ADR,
  output [7:0] OUT_0,
  output [7:0] OUT_1,
  output [7:0] OUT_2,
  output [7:0] OUT_3,
  output [7:0] OUT_4,
  output [7:0] OUT_5,
  output [7:0] OUT_6,
  output [7:0] OUT_7
);

  wire and_1_out, and_2_out, and_3_out, and_4_out, and_5_out, and_6_out, and_7_out, and_8_out,
       comparator_1_eq, comparator_2_eq, comparator_3_eq, comparator_4_eq, comparator_5_eq, comparator_6_eq,
       comparator_7_eq, comparator_8_eq, comparator_9_eq;

  Comparator #(.Bits(8)) comparator_1 (.a(CMD), .b(8'h2b), .eq(comparator_1_eq));  // open: gt, lt
  Comparator #(.Bits(8)) comparator_2 (.a(ADR[7:0]), .b({8{1'b0}}), .eq(comparator_2_eq));  // open: gt, lt
  Comparator #(.Bits(8)) comparator_3 (.a(ADR[7:0]), .b(8'h1), .eq(comparator_3_eq));  // open: gt, lt
  Comparator #(.Bits(8)) comparator_4 (.a(ADR[7:0]), .b(8'h2), .eq(comparator_4_eq));  // open: gt, lt
  Comparator #(.Bits(8)) comparator_5 (.a(ADR[7:0]), .b(8'h3), .eq(comparator_5_eq));  // open: gt, lt
  and and_1 (and_1_out, comparator_1_eq, comparator_2_eq);
  and and_2 (and_2_out, comparator_1_eq, comparator_3_eq);
  and and_3 (and_3_out, comparator_1_eq, comparator_4_eq);
  and and_4 (and_4_out, comparator_1_eq, comparator_5_eq);
  Register #(.Bits(8)) register_1 (.D(DAT), .C(and_1_out), .en(1'b1), .Q(OUT_0));
  Register #(.Bits(8)) register_2 (.D(DAT), .C(and_2_out), .en(1'b1), .Q(OUT_1));
  Register #(.Bits(8)) register_3 (.D(DAT), .C(and_3_out), .en(1'b1), .Q(OUT_2));
  Register #(.Bits(8)) register_4 (.D(DAT), .C(and_4_out), .en(1'b1), .Q(OUT_3));
  Comparator #(.Bits(8)) comparator_6 (.a(ADR[7:0]), .b(8'h4), .eq(comparator_6_eq));  // open: gt, lt
  Comparator #(.Bits(8)) comparator_7 (.a(ADR[7:0]), .b(8'h5), .eq(comparator_7_eq));  // open: gt, lt
  Comparator #(.Bits(8)) comparator_8 (.a(ADR[7:0]), .b(8'h6), .eq(comparator_8_eq));  // open: gt, lt
  Comparator #(.Bits(8)) comparator_9 (.a(ADR[7:0]), .b(8'h7), .eq(comparator_9_eq));  // open: gt, lt
  and and_5 (and_5_out, comparator_1_eq, comparator_6_eq);
  and and_6 (and_6_out, comparator_1_eq, comparator_7_eq);
  and and_7 (and_7_out, comparator_1_eq, comparator_8_eq);
  and and_8 (and_8_out, comparator_1_eq, comparator_9_eq);
  Register #(.Bits(8)) register_5 (.D(DAT), .C(and_5_out), .en(1'b1), .Q(OUT_4));
  Register #(.Bits(8)) register_6 (.D(DAT), .C(and_6_out), .en(1'b1), .Q(OUT_5));
  Register #(.Bits(8)) register_7 (.D(DAT), .C(and_7_out), .en(1'b1), .Q(OUT_6));
  Register #(.Bits(8)) register_8 (.D(DAT), .C(and_8_out), .en(1'b1), .Q(OUT_7));

  // Notes on the sheet:
  //   ADR
  //   DAT
  //   EN
  //   these splitters just discard
  //   the last 8 bits of the address bus
endmodule
