// Digital circuit ALU.dig as structural Verilog
module ALU (
  input  CLK,
  output [7:0] Q,
  output DAT_dis
);

  wire _8_input_or_1_p2, _8_input_or_2_p2, adder_subtractor_1_c_8, adder_subtractor_1_f,
       adder_subtractor_1_stc, adder_subtractor_1_stf, comparator_1_eq, comparator_2_eq, comparator_3_eq,
       comparator_4_eq, comparator_5_eq, comparator_6_eq, comparator_7_eq, comparator_8_eq, comparator_9_eq,
       comparator_10_eq, comparator_11_eq, comparator_12_eq, comparator_13_eq, comparator_14_eq,
       comparator_15_eq, comparator_16_eq, comparator_17_eq, comparator_18_eq, comparator_19_eq,
       comparator_20_eq, comparator_21_eq, comparator_22_eq, comparator_24_eq, comparator_25_eq,
       comparator_26_eq, comparator_27_eq, comparator_28_eq, comparator_29_eq, comparator_30_eq,
       comparator_31_eq, flag_register_1_c;
  wire [7:0] flash_memory_1_q_cmd, register_1_val, register_2_val, register_3_val, register_4_val;
  wire [15:0] programme_counter_1_ln;

  Programme_Counter programme_counter_1 (
    .DAT(Q), .ADR({16{1'b0}}), .CLK(CLK), .JMP(1'b0), .CJP(1'b0), .CLR(1'b0), .LN(programme_counter_1_ln));
  Flash_Memory flash_memory_1 (
    .LN(programme_counter_1_ln), .DAT_dis(DAT_dis), .ADR_dis(1'b0), .CLK(CLK), .Q_CMD(flash_memory_1_q_cmd),
    .Q_DAT(Q));  // open: Q_ADR
  Comparator #(.Bits(8)) comparator_1 (.a(flash_memory_1_q_cmd), .b(8'h18), .eq(comparator_1_eq));  // open: gt, lt
  Comparator #(.Bits(8)) comparator_2 (.a(flash_memory_1_q_cmd), .b(8'h19), .eq(comparator_2_eq));  // open: gt, lt
  Comparator #(.Bits(8)) comparator_3 (.a(flash_memory_1_q_cmd), .b(8'h1a), .eq(comparator_3_eq));  // open: gt, lt
  Comparator #(.Bits(8)) comparator_4 (.a(flash_memory_1_q_cmd), .b(8'h1b), .eq(comparator_4_eq));  // open: gt, lt
  Comparator #(.Bits(8)) comparator_5 (.a(flash_memory_1_q_cmd), .b(8'h1c), .eq(comparator_5_eq));  // open: gt, lt
  Comparator #(.Bits(8)) comparator_6 (.a(flash_memory_1_q_cmd), .b(8'h1d), .eq(comparator_6_eq));  // open: gt, lt
  DiodeForward diodeforward_1 (.in(comparator_2_eq), .out(DAT_dis));
  DiodeForward diodeforward_2 (.in(comparator_4_eq), .out(DAT_dis));
  DiodeForward diodeforward_3 (.in(comparator_6_eq), .out(DAT_dis));
  PullDown pulldown_1 (.out(DAT_dis));
  Register register_1 (.D(Q), .STR(comparator_1_eq), .LD(comparator_2_eq), .CLK(CLK), .VAL(register_1_val), .Q(Q));
  Register register_2 (.D(Q), .STR(comparator_3_eq), .LD(comparator_4_eq), .CLK(CLK), .VAL(register_2_val), .Q(Q));
  Register register_3 (.D(Q), .STR(comparator_5_eq), .LD(comparator_6_eq), .CLK(CLK), .VAL(register_3_val), .Q(Q));
  Comparator #(.Bits(8)) comparator_7 (.a(flash_memory_1_q_cmd), .b(8'h1e), .eq(comparator_7_eq));  // open: gt, lt
  Comparator #(.Bits(8)) comparator_8 (.a(flash_memory_1_q_cmd), .b(8'h1f), .eq(comparator_8_eq));  // open: gt, lt
  Comparator #(.Bits(8)) comparator_9 (.a(flash_memory_1_q_cmd), .b(8'h20), .eq(comparator_9_eq));  // open: gt, lt
  Comparator #(.Bits(8)) comparator_10 (.a(flash_memory_1_q_cmd), .b(8'h21), .eq(comparator_10_eq));  // open: gt, lt
  Comparator #(.Bits(8)) comparator_11 (.a(flash_memory_1_q_cmd), .b(8'h8), .eq(comparator_11_eq));  // open: gt, lt
  Comparator #(.Bits(8)) comparator_12 (.a(flash_memory_1_q_cmd), .b(8'h9), .eq(comparator_12_eq));  // open: gt, lt
  Comparator #(.Bits(8)) comparator_13 (.a(flash_memory_1_q_cmd), .b(8'ha), .eq(comparator_13_eq));  // open: gt, lt
  Comparator #(.Bits(8)) comparator_14 (.a(flash_memory_1_q_cmd), .b(8'hb), .eq(comparator_14_eq));  // open: gt, lt
  Comparator #(.Bits(8)) comparator_15 (.a(flash_memory_1_q_cmd), .b(8'hc), .eq(comparator_15_eq));  // open: gt, lt
  Comparator #(.Bits(8)) comparator_16 (.a(flash_memory_1_q_cmd), .b(8'h15), .eq(comparator_16_eq));  // open: gt, lt
  Comparator #(.Bits(8)) comparator_17 (.a(flash_memory_1_q_cmd), .b(8'h16), .eq(comparator_17_eq));  // open: gt, lt
  Comparator #(.Bits(8)) comparator_18 (.a(flash_memory_1_q_cmd), .b(8'h17), .eq(comparator_18_eq));  // open: gt, lt
  Comparator #(.Bits(8)) comparator_19 (.a(flash_memory_1_q_cmd), .b(8'h22), .eq(comparator_19_eq));  // open: gt, lt
  Comparator #(.Bits(8)) comparator_20 (.a(flash_memory_1_q_cmd), .b(8'h23), .eq(comparator_20_eq));  // open: gt, lt
  Comparator #(.Bits(8)) comparator_21 (.a(flash_memory_1_q_cmd), .b(8'h24), .eq(comparator_21_eq));  // open: gt, lt
  Comparator #(.Bits(8)) comparator_22 (.a(flash_memory_1_q_cmd), .b(8'h25), .eq(comparator_22_eq));  // open: gt, lt
  DiodeForward diodeforward_4 (.in(comparator_8_eq), .out(DAT_dis));
  DiodeForward diodeforward_5 (.in(comparator_9_eq), .out(DAT_dis));
  DiodeForward diodeforward_6 (.in(comparator_10_eq), .out(DAT_dis));
  DiodeForward diodeforward_7 (.in(comparator_11_eq), .out(DAT_dis));
  DiodeForward diodeforward_8 (.in(comparator_12_eq), .out(DAT_dis));
  DiodeForward diodeforward_9 (.in(comparator_13_eq), .out(DAT_dis));
  DiodeForward diodeforward_10 (.in(comparator_14_eq), .out(DAT_dis));
  DiodeForward diodeforward_11 (.in(comparator_15_eq), .out(DAT_dis));
  DiodeForward diodeforward_12 (.in(comparator_16_eq), .out(DAT_dis));
  DiodeForward diodeforward_13 (.in(comparator_17_eq), .out(DAT_dis));
  DiodeForward diodeforward_14 (.in(comparator_18_eq), .out(DAT_dis));
  DiodeForward diodeforward_15 (.in(comparator_21_eq), .out(DAT_dis));
  DiodeForward diodeforward_16 (.in(comparator_22_eq), .out(DAT_dis));
  PullDown pulldown_2 (.out(DAT_dis));
  Flag_Register flag_register_1 (
    .DAT(Q), .C_8(adder_subtractor_1_c_8), .F(adder_subtractor_1_f), .STC(adder_subtractor_1_stc),
    .STF(adder_subtractor_1_stf), .STA(comparator_7_eq), .LDC(comparator_8_eq), .LDF(comparator_9_eq),
    .LDA(comparator_10_eq), .CLK(CLK), .Q(Q), .C(flag_register_1_c));
  Adder_Subtractor adder_subtractor_1 (
    .C_in(flag_register_1_c), .A(register_1_val), .B(register_2_val), .ADD(comparator_11_eq),
    .ADC(comparator_12_eq), .SUB(comparator_13_eq), .CLK(CLK), .Q(Q), .C_8(adder_subtractor_1_c_8),
    .F(adder_subtractor_1_f), .STC(adder_subtractor_1_stc), .STF(adder_subtractor_1_stf));
  Incrementor incrementor_1 (
    .C(register_3_val), .INC(comparator_14_eq), .DEC(comparator_15_eq), .CLK(CLK), .Q(Q),
    .C_8(adder_subtractor_1_c_8), .F(adder_subtractor_1_f), .STC(adder_subtractor_1_stc),
    .STF(adder_subtractor_1_stf));  // open: Q_S
  Comparator comparator_23 (
    .A(register_1_val), .B(register_2_val), .CMP_bigger(comparator_16_eq), .CMP_equal(comparator_17_eq),
    .CMP_smaller(comparator_18_eq), .CLK(CLK), .Q(Q));
  Register register_4 (.D(Q), .STR(comparator_19_eq), .LD(comparator_20_eq), .CLK(CLK), .VAL(register_4_val), .Q(Q));
  Barrel_Shift_Register barrel_shift_register_1 (
    .A(register_1_val), .DIS(register_4_val), .SFT(comparator_21_eq), .SFC(comparator_22_eq), .CLK(CLK), .Q(Q));
  Comparator #(.Bits(8)) comparator_24 (.a(flash_memory_1_q_cmd), .b(8'hd), .eq(comparator_24_eq));  // open: gt, lt
  Comparator #(.Bits(8)) comparator_25 (.a(flash_memory_1_q_cmd), .b(8'he), .eq(comparator_25_eq));  // open: gt, lt
  Comparator #(.Bits(8)) comparator_26 (.a(flash_memory_1_q_cmd), .b(8'hf), .eq(comparator_26_eq));  // open: gt, lt
  Comparator #(.Bits(8)) comparator_27 (.a(flash_memory_1_q_cmd), .b(8'h10), .eq(comparator_27_eq));  // open: gt, lt
  Comparator #(.Bits(8)) comparator_28 (.a(flash_memory_1_q_cmd), .b(8'h11), .eq(comparator_28_eq));  // open: gt, lt
  Comparator #(.Bits(8)) comparator_29 (.a(flash_memory_1_q_cmd), .b(8'h12), .eq(comparator_29_eq));  // open: gt, lt
  Comparator #(.Bits(8)) comparator_30 (.a(flash_memory_1_q_cmd), .b(8'h13), .eq(comparator_30_eq));  // open: gt, lt
  Comparator #(.Bits(8)) comparator_31 (.a(flash_memory_1_q_cmd), .b(8'h14), .eq(comparator_31_eq));  // open: gt, lt
  DiodeForward diodeforward_17 (.in(comparator_24_eq), .out(DAT_dis));
  DiodeForward diodeforward_18 (.in(comparator_25_eq), .out(DAT_dis));
  DiodeForward diodeforward_19 (.in(comparator_26_eq), .out(DAT_dis));
  DiodeForward diodeforward_20 (.in(comparator_27_eq), .out(DAT_dis));
  DiodeForward diodeforward_21 (.in(comparator_28_eq), .out(DAT_dis));
  DiodeForward diodeforward_22 (.in(comparator_29_eq), .out(DAT_dis));
  DiodeForward diodeforward_23 (.in(comparator_30_eq), .out(DAT_dis));
  DiodeForward diodeforward_24 (.in(comparator_31_eq), .out(DAT_dis));
  PullDown pulldown_3 (.out(DAT_dis));
  // _8_Input_Or _8_input_or_1: pin names not known; wires that end beside it: register_1_val, _8_input_or_1_p2
  // _8_Input_Or _8_input_or_2: pin names not known; wires that end beside it: register_2_val, _8_input_or_2_p2
  Binary_NOT binary_not_1 (.A(_8_input_or_1_p2), .EN(comparator_24_eq), .CLK(CLK), .Q(Q));
  Binary_OR binary_or_1 (.A(_8_input_or_1_p2), .B(_8_input_or_2_p2), .EN(comparator_25_eq), .CLK(CLK), .Q(Q));
  Binary_AND binary_and_1 (.A(_8_input_or_1_p2), .B(_8_input_or_2_p2), .EN(comparator_26_eq), .CLK(CLK), .Q(Q));
  Binary_XOR binary_xor_1 (.A(_8_input_or_1_p2), .B(_8_input_or_2_p2), .EN(comparator_27_eq), .CLK(CLK), .Q(Q));
  Bitwise_NOT bitwise_not_1 (.A(register_1_val), .EN(comparator_28_eq), .CLK(CLK), .Q(Q));
  Bitwise_OR bitwise_or_1 (.A(register_1_val), .B(register_2_val), .EN(comparator_29_eq), .CLK(CLK));  // open: Q
  Bitwise_AND bitwise_and_1 (.A(register_1_val), .B(register_2_val), .EN(comparator_30_eq), .CLK(CLK), .Q(Q));
  Bitwise_XOR bitwise_xor_1 (.A(register_1_val), .B(register_2_val), .EN(comparator_31_eq), .CLK(CLK), .Q(Q));

  // Notes on the sheet:
  //   CMD
  //   DAT
  //   CLK
  //   A
  //   B
  //   C
  //   Q
  //   DAT_dis
  //   putting these signals together
  //   without any or gates or diodes
  //   might be possible, as the buffers
  //   should have protection against
  //   that
endmodule
