// Digital circuit Adder Subtractor.dig as structural Verilog
module Adder_Subtractor (
  input  [7:0] A,
  input  [7:0] B,
  input  ADD,
  input  C_in,
  input  SUB,
  input  CLK,
  output [7:0] Q,
  output C_8,
  output F
);

  wire add_1_c_o, add_2_c_o, d_ff_2_q, not_1_out, or_1_out, or_2_out, xor_2_out;
  wire [6:0] add_1_s;
  wire [7:0] xor_1_out;
  wire [7:7] add_2_s, d_ff_1_q;

  not not_1 (not_1_out, CLK);
  or or_1 (or_1_out, ADD, SUB);
  D_FF d_ff_1 (.D(SUB), .C(not_1_out), .Q(d_ff_1_q[7]));  // open: nQ
  D_FF d_ff_2 (.D(or_1_out), .C(not_1_out), .Q(d_ff_2_q));  // open: nQ
  or or_2 (or_2_out, C_in, d_ff_1_q[7]);
  assign xor_1_out = B ^ {8{d_ff_1_q[7]}};  // XOr xor_1, 8 bits wide
  Add #(.Bits(7)) add_1 (.a(A[6:0]), .b(xor_1_out[6:0]), .c_i(or_2_out), .s(add_1_s), .c_o(add_1_c_o));
  Add add_2 (.a(A[7]), .b(xor_1_out[7]), .c_i(add_1_c_o), .s(add_2_s[7]), .c_o(add_2_c_o));
  xor xor_2 (xor_2_out, add_1_c_o, add_2_c_o);
  // _8bit_Bus_Interface _8bit_bus_interface_1: pin names not known; wires that end beside it: {add_2_s[7], add_1_s}, d_ff_2_q, Q
  _1bit_Bus_Interface _1bit_bus_interface_1 (.Q(C_8), .IN(add_2_c_o), .EN(d_ff_2_q));
  _1bit_Bus_Interface _1bit_bus_interface_2 (.Q(F), .IN(xor_2_out), .EN(d_ff_2_q));

  // Notes on the sheet:
  //   The sub d-lach needs the command from
  //   the previous cycle and the new clock pulse 
  //   to be there simultaneously
  //   An XOR gate inverts one input if the other one
  //   is high. This is needed for 2's complement subtraction.
  //   Makes sure that 
  //   every XOR gate 
  //   has SUB as an 
  //   input, since it is 
  //   8bit wide it will only 
  //   accept 8bit inputs.
  //   The split adder + the xor gate are for 
  //   Overflow detection during a subtraction
  //   -> the normal 8bit output
  //   -> the carry output incase the adder output exceeds the 8 bit limit
  //   -> overflow of the subtractor
endmodule
