// Digital circuit Binary AND.dig as structural Verilog
module Binary_AND (
  input  A,
  input  B,
  input  EN,
  input  CLK,
  output [7:0] Q
);

  wire and_1_out, d_ff_1_q, not_1_out;
  wire [0:0] d_ff_2_q;

  not not_1 (not_1_out, CLK);
  D_FF d_ff_1 (.D(EN), .C(not_1_out), .Q(d_ff_1_q));  // open: nQ
  and and_1 (and_1_out, A, B);
  D_FF d_ff_2 (.D(and_1_out), .C(d_ff_1_q), .Q(d_ff_2_q[0]));  // open: nQ
  assign Q = d_ff_1_q ? {{7{1'b0}}, d_ff_2_q[0]} : 8'bz;  // Driver driver_1
endmodule
