// Digital circuit Binary NOT.dig as structural Verilog
module Binary_NOT (
  input  [7:0] A,
  input  CLK,
  input  EN,
  output [7:0] Q
);

  wire d_ff_1_q, d_ff_2_q, or_1_out;
  wire [0:0] not_1_out;

  or or_1 (or_1_out, A[0], A[1], A[2], A[3], A[4], A[5], A[6], A[7]);
  not not_1 (not_1_out[0], or_1_out);
  D_FF d_ff_1 (.D(EN), .C(CLK), .Q(d_ff_1_q));  // open: nQ
  D_FF d_ff_2 (.D(d_ff_1_q), .C(CLK), .Q(d_ff_2_q));  // open: nQ
  assign Q = d_ff_2_q ? {{7{1'b0}}, not_1_out[0]} : 8'bz;  // Driver driver_1
endmodule
