// Digital circuit Bitwise NOT.dig as structural Verilog
module Bitwise_NOT (
  input  [7:0] A,
  input  EN,
  input  CLK,
  output [7:0] Q
);

  wire d_ff_1_q, d_ff_2_q;
  wire [7:0] not_1_out;

  assign not_1_out = ~A;  // Not not_1, 8 bits wide
  D_FF d_ff_1 (.D(EN), .C(CLK), .Q(d_ff_1_q));  // open: nQ
  D_FF d_ff_2 (.D(d_ff_1_q), .C(CLK), .Q(d_ff_2_q));  // open: nQ
  assign Q = d_ff_2_q ? not_1_out : 8'bz;  // Driver driver_1
endmodule
