// Digital circuit Flag Register.dig as structural Verilog
module Flag_Register (
  input  [7:0] DAT,
  input  C_8,
  input  F,
  input  STC,
  input  STB,
  input  LDC,
  input  LDF,
  input  LDA,
  input  CLK,
  input  STF,
  output [7:0] Q,
  output C_8_2
);

  wire and_1_out, and_2_out, and_3_out, and_4_out, not_1_out, or_1_out, or_2_out;
  wire [0:0] d_ff_1_q;

  not not_1 (not_1_out, CLK);
  and and_1 (and_1_out, DAT[0], STB);
  and and_2 (and_2_out, C_8, STC);
  and and_3 (and_3_out, DAT[1], STB);
  and and_4 (and_4_out, F, STF);
  or or_1 (or_1_out, and_1_out, and_2_out);
  or or_2 (or_2_out, and_3_out, and_4_out);
  D_FF d_ff_1 (.D(or_1_out), .C(not_1_out), .Q(d_ff_1_q[0]));  // open: nQ
  D_FF d_ff_2 (.D(or_2_out), .C(not_1_out), .Q(C_8_2));  // open: nQ
  assign Q = LDA ? {{6{1'b0}}, C_8_2, d_ff_1_q[0]} : 8'bz;  // Driver driver_1
  assign Q[0] = LDC ? d_ff_1_q[0] : 1'bz;  // Driver driver_2
  assign Q[0] = LDF ? C_8_2 : 1'bz;  // Driver driver_3
  // also tied to GND on the sheet: {Q[1], Q[2], Q[3], Q[4], Q[5], Q[6], Q[7]}

  // Notes on the sheet:
  //   DAT: connection to the data bus
  //   C_8: carry out from the adder
  //   F: oveflow from the subtractor
  //   STC: store carry
  //   STF: store overflow
  //   STB: store from bus
  //   LDC: load carry
  //   LDF: load overflow
  //   LDA: load all
  //   CLK: clock input
endmodule
