// Digital circuit Flash Memory.dig as structural Verilog
module Flash_Memory (
  input  [15:0] LN,
  input  DAT_dis,
  input  ADR_dis,
  input  CLK,
  output [7:0] Q_CMD,
  output [7:0] Q_DAT,
  output [15:0] Q_ADR
);

  wire d_ff_1_q, d_ff_2_q, d_ff_3_q, d_ff_4_q, not_1_out, not_2_out, not_3_out, or_1_out, or_2_out;
  wire [7:0] DAT_d;
  wire [15:0] ADR_d;

  not not_1 (not_1_out, CLK);
  D_FF d_ff_1 (.D(DAT_dis), .C(not_1_out), .Q(d_ff_1_q));  // open: nQ
  D_FF d_ff_2 (.D(ADR_dis), .C(not_1_out), .Q(d_ff_2_q));  // open: nQ
  D_FF d_ff_3 (.D(d_ff_1_q), .C(CLK), .Q(d_ff_3_q));  // open: nQ
  D_FF d_ff_4 (.D(d_ff_2_q), .C(CLK), .Q(d_ff_4_q));  // open: nQ
  or or_1 (or_1_out, d_ff_3_q, d_ff_1_q);
  or or_2 (or_2_out, d_ff_4_q, d_ff_2_q);
  not not_2 (not_2_out, or_1_out);
  not not_3 (not_3_out, or_2_out);
  ROM #(.AddrBits(16), .isProgramMemory("true"), .Bits(8)) CMD (.A(LN), .sel(1'b1), .D(Q_CMD));
  ROM #(.AddrBits(16), .isProgramMemory("true"), .Bits(8)) DAT (.A(LN), .sel(1'b1), .D(DAT_d));
  ROM #(.AddrBits(16), .isProgramMemory("true"), .Bits(16)) ADR (.A(LN), .sel(1'b1), .D(ADR_d));
  assign Q_DAT = not_2_out ? DAT_d : 8'bz;  // Driver driver_1
  assign Q_ADR = not_3_out ? ADR_d : 16'bz;  // Driver driver_2

  // Notes on the sheet:
  //   DAT_dis / ADR_dis :
  //   disable the data / address bus
  //   for the next tick in order to
  //   avoid bus collisions
  //   the clock is delayed in order to wait
  //   for commands to send their disable 
  //   signals before they get saved in order
  //   to instantly stop output to the buses
  //   - at least 16ns delay
  //   contents of CMD (hex, n*v repeats v):
  //   0,6,0,7,18,1a,8,1a,18,a,18,9,1c,b,18,1a,16,22,18,25,28,1
  //   contents of DAT (hex, n*v repeats v):
  //   0,1,0,0,0,2,0,0,fd,6*0,ff,0,0,1
  //   contents of ADR (hex, n*v repeats v):
  //   0,1,2,1
endmodule
