// Digital circuit Incrementor.dig as structural Verilog
module Incrementor (
  input  [7:0] C,
  input  INC,
  input  DEC,
  input  CLK,
  output [7:0] Q,
  output C_8,
  output F,
  output STC,
  output STF,
  output Q_S
);

  wire add_1_c_o, add_2_c_o, d_ff_1_q, d_ff_2_q, d_ff_3_q, d_ff_4_nq, d_ff_4_q, not_1_out, or_1_out,
       xor_2_out;
  wire [6:0] add_1_s;
  wire [7:0] register_1_q, xor_1_out;
  wire [7:7] add_2_s;

  not not_1 (not_1_out, CLK);
  or or_1 (or_1_out, INC, DEC);
  D_FF d_ff_1 (.D(or_1_out), .C(not_1_out), .Q(d_ff_1_q));  // open: nQ
  assign xor_1_out = {8{DEC}} ^ 8'h1;  // XOr xor_1, 8 bits wide
  and and_1 (Q_S, d_ff_1_q, CLK);
  Add #(.Bits(7)) add_1 (.a(C[6:0]), .b(xor_1_out[6:0]), .c_i(DEC), .s(add_1_s), .c_o(add_1_c_o));
  Add add_2 (.a(C[7]), .b(xor_1_out[7]), .c_i(add_1_c_o), .s(add_2_s[7]), .c_o(add_2_c_o));
  xor xor_2 (xor_2_out, add_1_c_o, add_2_c_o);
  Register #(.Bits(8)) register_1 (.D({add_2_s[7], add_1_s}), .C(d_ff_1_q), .en(1'b1), .Q(register_1_q));
  D_FF d_ff_2 (.D(add_2_c_o), .C(d_ff_1_q), .Q(d_ff_2_q));  // open: nQ
  D_FF d_ff_3 (.D(xor_2_out), .C(d_ff_1_q), .Q(d_ff_3_q));  // open: nQ
  D_FF d_ff_4 (.D(DEC), .C(d_ff_1_q), .Q(d_ff_4_q), .nQ(d_ff_4_nq));
  assign Q = d_ff_1_q ? register_1_q : 8'bz;  // Driver driver_1
  assign C_8 = d_ff_1_q ? d_ff_2_q : 1'bz;  // Driver driver_2
  assign F = d_ff_1_q ? d_ff_3_q : 1'bz;  // Driver driver_3
  assign STC = d_ff_1_q ? d_ff_4_q : 1'bz;  // Driver driver_4
  assign STF = d_ff_1_q ? d_ff_4_nq : 1'bz;  // Driver driver_5

  // Notes on the sheet:
  //   -> the normal 8bit output
  //   -> the carry output incase the adder 
  //   output exceeds the 8 bit limit
  //   -> overflow of the subtractor
  //   -> store the carry bit to the
  //   flags register
  //   -> store the overflow bit to the
  //   flags register
  //   -> save the output to the C register
endmodule
