// Digital circuit Input Control.dig as structural Verilog
module Input_Control (
  input  INP,
  input  LD,
  input  CLK,
  output [7:0] Q
);

  wire d_ff_1_q, d_ff_2_q, not_1_out, rs_ff_as_1_q;

  not not_1 (not_1_out, CLK);
  RS_FF_AS rs_ff_as_1 (.S(INP), .R(d_ff_2_q), .Q(rs_ff_as_1_q));  // open: nQ
  D_FF d_ff_1 (.D(LD), .C(not_1_out), .Q(d_ff_1_q));  // open: nQ
  D_FF d_ff_2 (.D(d_ff_1_q), .C(not_1_out), .Q(d_ff_2_q));  // open: nQ
  assign Q[0] = d_ff_1_q ? rs_ff_as_1_q : 1'bz;  // Driver driver_1

  assign Q[7:1] = {7{1'b0}};

  // Notes on the sheet:
  //   INP - input > sets the sr reg to high
  //   to indicate the input reg has been 
  //   written to
endmodule
