// Digital circuit Programme Counter.dig as structural Verilog
module Programme_Counter (
  input  [7:0] DAT,
  input  [15:0] ADR,
  input  CLK,
  input  JMP,
  input  CJP,
  input  CLR,
  output [15:0] LN
);

  wire _8_input_or_1_p2, and_1_out, d_ff_1_q, or_1_out;

  // _8_Input_Or _8_input_or_1: pin names not known; wires that end beside it: DAT, _8_input_or_1_p2
  D_FF d_ff_1 (.D(_8_input_or_1_p2), .C(CJP), .Q(d_ff_1_q));  // open: nQ
  and and_1 (and_1_out, d_ff_1_q, CJP);
  or or_1 (or_1_out, JMP, and_1_out);
  CounterPreset #(.maxValue(65535), .Bits(16), .isProgramCounter("true")) counterpreset_1 (
    .en(1'b1), .C(CLK), .dir(1'b0), .in(ADR), .ld(or_1_out), .clr(CLR), .out(LN));  // open: ovf

  // Notes on the sheet:
  //   DAT: Data input
  //   ADR: Address input
  //   CLK: Clock input
  //   JMP: Jump command
  //   CJP: Conditional Jump command
  //   CLR: Clear for starting the CPU
endmodule
