// Digital circuit Shift Register.dig as structural Verilog
module Shift_Register (
  input  in_1,
  input  in_2,
  input  in_3,
  input  in_4,
  input  in_5,
  input  in_6,
  input  in_7,
  input  in_8,
  input  in_9,
  input  in_10,
  input  in_11,
  output out_12,
  output out_13,
  output out_14,
  output out_15,
  output out_16,
  output out_17,
  output out_18,
  output out_19
);

  wire multiplexer_1_out, multiplexer_2_out, multiplexer_3_out, multiplexer_4_out, multiplexer_5_out,
       multiplexer_6_out, multiplexer_7_out, multiplexer_8_out, multiplexer_9_out, multiplexer_10_out,
       multiplexer_11_out, multiplexer_12_out, multiplexer_13_out, multiplexer_14_out, multiplexer_15_out,
       multiplexer_16_out;

  Multiplexer multiplexer_1 (.sel(in_9), .in_0(in_1), .in_1(in_2), .out(multiplexer_1_out));
  Multiplexer multiplexer_2 (.sel(in_9), .in_0(in_2), .in_1(in_3), .out(multiplexer_2_out));
  Multiplexer multiplexer_3 (.sel(in_9), .in_0(in_3), .in_1(in_4), .out(multiplexer_3_out));
  Multiplexer multiplexer_4 (.sel(in_9), .in_0(in_4), .in_1(in_5), .out(multiplexer_4_out));
  Multiplexer multiplexer_5 (.sel(in_9), .in_0(in_5), .in_1(in_6), .out(multiplexer_5_out));
  Multiplexer multiplexer_6 (.sel(in_9), .in_0(in_6), .in_1(in_7), .out(multiplexer_6_out));
  Multiplexer multiplexer_7 (.sel(in_9), .in_0(in_7), .in_1(in_8), .out(multiplexer_7_out));
  Multiplexer multiplexer_8 (.sel(in_9), .in_0(in_8), .in_1(1'b0), .out(multiplexer_8_out));
  Multiplexer multiplexer_9 (.sel(in_10), .in_0(multiplexer_1_out), .in_1(multiplexer_3_out), .out(multiplexer_9_out));
  Multiplexer multiplexer_10 (
    .sel(in_10), .in_0(multiplexer_2_out), .in_1(multiplexer_4_out), .out(multiplexer_10_out));
  Multiplexer multiplexer_11 (
    .sel(in_10), .in_0(multiplexer_3_out), .in_1(multiplexer_5_out), .out(multiplexer_11_out));
  Multiplexer multiplexer_12 (
    .sel(in_10), .in_0(multiplexer_4_out), .in_1(multiplexer_6_out), .out(multiplexer_12_out));
  Multiplexer multiplexer_13 (
    .sel(in_10), .in_0(multiplexer_5_out), .in_1(multiplexer_7_out), .out(multiplexer_13_out));
  Multiplexer multiplexer_14 (
    .sel(in_10), .in_0(multiplexer_6_out), .in_1(multiplexer_8_out), .out(multiplexer_14_out));
  Multiplexer multiplexer_15 (.sel(in_10), .in_0(multiplexer_7_out), .in_1(1'b0), .out(multiplexer_15_out));
  Multiplexer multiplexer_16 (.sel(in_10), .in_0(multiplexer_8_out), .in_1(1'b0), .out(multiplexer_16_out));
  Multiplexer multiplexer_17 (.sel(in_11), .in_0(multiplexer_9_out), .in_1(multiplexer_13_out), .out(out_12));
  Multiplexer multiplexer_18 (.sel(in_11), .in_0(multiplexer_10_out), .in_1(multiplexer_14_out), .out(out_13));
  Multiplexer multiplexer_19 (.sel(in_11), .in_0(multiplexer_11_out), .in_1(multiplexer_15_out), .out(out_14));
  Multiplexer multiplexer_20 (.sel(in_11), .in_0(multiplexer_12_out), .in_1(multiplexer_16_out), .out(out_15));
  Multiplexer multiplexer_21 (.sel(in_11), .in_0(multiplexer_13_out), .in_1(1'b0), .out(out_16));
  Multiplexer multiplexer_22 (.sel(in_11), .in_0(multiplexer_14_out), .in_1(1'b0), .out(out_17));
  Multiplexer multiplexer_23 (.sel(in_11), .in_0(multiplexer_15_out), .in_1(1'b0), .out(out_18));
  Multiplexer multiplexer_24 (.sel(in_11), .in_0(multiplexer_16_out), .in_1(1'b0), .out(out_19));
endmodule
